// Logisim project RyanKellarLALU.circ as structural Verilog: 22 circuits, main circuit R0R1
module R0R1 (
  input  in_1,
  input  [15:0] D,
  input  op,
  output [15:0] out_4
);

  wire clk;
  wire [15:0] R0_q, R1_q;

  Clock clock_1 (.out(clk));
  Register #(.width(16)) R0 (.D(out_4), .en(1'b1), .clk(clk), .Q(R0_q), .clr(in_1));
  Register #(.width(16)) R1 (.D(D), .en(1'b1), .clk(clk), .Q(R1_q), .clr(in_1));
  SixteenBitAddSubtract sixteenbitaddsubtract_1 (.a(R0_q), .b(R1_q), .op(op), .S(out_4));  // open: overflow

  // Other names for the same wires on the sheet: rst = in_1
endmodule

module SixteenBitAddSubtract (
  input  [15:0] a,
  input  [15:0] b,
  input  op,
  output overflow,
  output [15:0] S
);

  determiningoverflow determiningoverflow_1 (.A(a[15]), .B(b[15]), .R(S[15]), .op(op), .overflow(overflow));
  sixteenbitcarryselect sixteenbitcarryselect_1 (.a(a), .b(b), .op(op), .S(S));  // open: Cout
endmodule

module sixteenbitcarryselect (
  input  [15:0] a,
  input  [15:0] b,
  input  op,
  output [15:0] S,
  output Cout
);

  wire eightbitadder0_1_cout, eightbitadder0_2_cout, eightbitadder1_1_cout;
  wire [7:0] eightbitadder0_1_s, eightbitadder1_1_s;
  wire [15:0] adder_1_out, multiplexer_1_out, not_1_out;

  Adder #(.width(16)) adder_1 (.a({16{1'b0}}), .b(not_1_out), .out(adder_1_out), .cin(op));  // open: cout
  assign not_1_out = ~b;  // NOT_Gate not_1, 16 bits wide
  Multiplexer #(.width(16)) multiplexer_1 (.in0(b), .in1(adder_1_out), .out(multiplexer_1_out), .sel(op));
  EightBitAdder1 eightbitadder1_1 (
    .a(a[15:8]), .b(multiplexer_1_out[15:8]), .S(eightbitadder1_1_s), .Cout(eightbitadder1_1_cout));
  EightBitAdder0 eightbitadder0_1 (
    .a(a[15:8]), .b(multiplexer_1_out[15:8]), .S(eightbitadder0_1_s), .Cout(eightbitadder0_1_cout));
  Multiplexer #(.width(8)) multiplexer_2 (
    .in0(eightbitadder0_1_s), .in1(eightbitadder1_1_s), .out(S[15:8]), .sel(eightbitadder0_2_cout));
  Multiplexer multiplexer_3 (
    .in0(eightbitadder0_1_cout), .in1(eightbitadder1_1_cout), .out(Cout), .sel(eightbitadder0_2_cout));
  EightBitAdder0 eightbitadder0_2 (.a(a[7:0]), .b(multiplexer_1_out[7:0]), .S(S[7:0]), .Cout(eightbitadder0_2_cout));

  // Notes on the sheet:
  //   10.5
  //   10.5
  //   10.5
  //   10.5
  //   13
  //   10.5
  //   13
  //   13
  //   13
  //   16BitCarrySelectAdder
  //   01/15/2025
  //   Ryan Kellar
endmodule

module FA0 (
  input  a,
  input  b,
  output S,
  output Cout
);

  wire nor_1_out;

  nor nor_1 (nor_1_out, a, b);
  and and_1 (Cout, a, b);
  nor nor_2 (S, nor_1_out, Cout);

  // Notes on the sheet:
  //   Cin
  //   Ryan Kellar
  //   FA0
  //   12/9/2024
endmodule

module FourBitAdder0 (
  input  [3:0] a,
  input  [3:0] b,
  output [3:0] S,
  output Cout
);

  wire fa0_1_cout, fao1_2_cout, fao2_1_cout;

  FAO1 fao1_1 (.a(b[3]), .b(a[3]), .Cin(fao1_2_cout), .S(S[3]), .Cout(Cout));
  FAO1 fao1_2 (.a(b[2]), .b(a[2]), .Cin(fao2_1_cout), .S(S[2]), .Cout(fao1_2_cout));
  FAO2 fao2_1 (.a(b[1]), .b(a[1]), .Cin(fa0_1_cout), .Cout(fao2_1_cout), .S(S[1]));
  FA0 fa0_1 (.a(b[0]), .b(a[0]), .S(S[0]), .Cout(fa0_1_cout));

  // Notes on the sheet:
  //   If Cin < 2.75 then 4.75 else Cin + 2.00
  //   If Cin < 2.75 then 5.5 else Cin + 2.75
  //   8.75
  //   9.5
  //   6.75
  //   4.75
  //   7.5
  //   5.5
  //   Ryan Kellar
  //   FourBitAdder0
  //   01/15/2025
  //   1.75
  //   9.5
  //   8.75
  //   2.75
  //   Cin + 2.25
  //   If Cin < 2.75 then 5.5 else Cin + 2.75
endmodule

module FourBitAdder1 (
  input  [3:0] a,
  input  [3:0] b,
  output [3:0] S,
  output Cout
);

  wire fa1_1_cout, fao1_2_cout, fao1_3_cout;

  FAO1 fao1_1 (.a(b[3]), .b(a[3]), .Cin(fao1_2_cout), .S(S[3]), .Cout(Cout));
  FAO1 fao1_2 (.a(b[2]), .b(a[2]), .Cin(fao1_3_cout), .S(S[2]), .Cout(fao1_2_cout));
  FAO1 fao1_3 (.a(b[1]), .b(a[1]), .Cin(fa1_1_cout), .S(S[1]), .Cout(fao1_3_cout));
  FA1 fa1_1 (.a(b[0]), .b(a[0]), .S(S[0]), .Cout(fa1_1_cout));

  // Notes on the sheet:
  //   Ryan Kellar
  //   FourBitAdder0
  //   01/15/2025
endmodule

module FAO1 (
  input  a,
  input  b,
  input  Cin,
  output S,
  output Cout
);

  wire nand_1_out, nand_2_out, nor_1_out, nor_2_out, nor_3_out, not_1_out, not_2_out;

  nand nand_1 (nand_1_out, a, b);
  nor nor_1 (nor_1_out, a, b);
  nor nor_2 (nor_2_out, nor_1_out, not_1_out);
  not not_1 (not_1_out, nand_1_out);
  nor nor_3 (nor_3_out, nor_2_out, Cin);
  nand nand_2 (nand_2_out, nor_2_out, Cin);
  not not_2 (not_2_out, nand_2_out);
  nand nand_3 (Cout, nand_2_out, nand_1_out);
  nor nor_4 (S, nor_3_out, not_2_out);

  // Notes on the sheet:
  //   1.00
  //   0.75
  //   1.00
  //   1.00
  //   1.00
  //   1.00
  //   0.75
  //   1.00
  //   1.00
  //   Ryan Kellar
  //   12/14/2024
  //   32 transistors
  //   1.00 + 0.75 + 1.00 + 1.00 + 0.75 + 1.00 = 5.5
  //   If Cin < 2.75 then 5.5 else Cin + 2.75
  //   1.00 + 0.75 + 1.00 + 1.00 + 1.00 = 4.75
  //   If Cin < 2.75 then 4.75 else Cin + 2.00
endmodule

module FA1 (
  input  a,
  input  b,
  output S,
  output Cout
);

  wire nand_1_out;

  or or_1 (Cout, a, b);
  nand nand_1 (nand_1_out, a, b);
  nand nand_2 (S, Cout, nand_1_out);

  // Notes on the sheet:
  //   Cin
  //   Ryan Kellar
  //   FA1
  //   12/11/2024
endmodule

module EightBitAdder0 (
  input  [7:0] a,
  input  [7:0] b,
  output [7:0] S,
  output Cout
);

  wire fourbitadder0_1_cout, fourbitadder0_2_cout, fourbitadder1_1_cout;
  wire [3:0] fourbitadder0_1_s, fourbitadder1_1_s;

  FourBitAdder1 fourbitadder1_1 (.a(a[7:4]), .b(b[7:4]), .S(fourbitadder1_1_s), .Cout(fourbitadder1_1_cout));
  FourBitAdder0 fourbitadder0_1 (.a(a[7:4]), .b(b[7:4]), .S(fourbitadder0_1_s), .Cout(fourbitadder0_1_cout));
  Multiplexer #(.width(4)) multiplexer_1 (
    .in0(fourbitadder0_1_s), .in1(fourbitadder1_1_s), .out(S[7:4]), .sel(fourbitadder0_2_cout));
  Multiplexer multiplexer_2 (
    .in0(fourbitadder0_1_cout), .in1(fourbitadder1_1_cout), .out(Cout), .sel(fourbitadder0_2_cout));
  FourBitAdder0 fourbitadder0_2 (.a(a[3:0]), .b(b[3:0]), .S(S[3:0]), .Cout(fourbitadder0_2_cout));

  // Notes on the sheet:
  //   8.75
  //   9.5
  //   8.75
  //   9.5
  //   8.75
  //   9.5
  //   Ryan Kellar
  //   EightBItAdder0
  //   01/15/2025
  //   10.5
  //   10.5
endmodule

module EightBitAdder1 (
  input  [7:0] a,
  input  [7:0] b,
  output [7:0] S,
  output Cout
);

  wire fourbitadder0_1_cout, fourbitadder1_1_cout, fourbitadder1_2_cout;
  wire [3:0] fourbitadder0_1_s, fourbitadder1_1_s;

  FourBitAdder1 fourbitadder1_1 (.a(a[7:4]), .b(b[7:4]), .S(fourbitadder1_1_s), .Cout(fourbitadder1_1_cout));
  FourBitAdder0 fourbitadder0_1 (.a(a[7:4]), .b(b[7:4]), .S(fourbitadder0_1_s), .Cout(fourbitadder0_1_cout));
  Multiplexer #(.width(4)) multiplexer_1 (
    .in0(fourbitadder0_1_s), .in1(fourbitadder1_1_s), .out(S[7:4]), .sel(fourbitadder1_2_cout));
  Multiplexer multiplexer_2 (
    .in0(fourbitadder0_1_cout), .in1(fourbitadder1_1_cout), .out(Cout), .sel(fourbitadder1_2_cout));
  FourBitAdder1 fourbitadder1_2 (.a(a[3:0]), .b(b[3:0]), .S(S[3:0]), .Cout(fourbitadder1_2_cout));

  // Notes on the sheet:
  //   Ryan Kellar
  //   EightBitAdder1
  //   01/15/2025
endmodule

module mx2i (
  input  in0,
  input  s0,
  input  in1,
  output z
);

  wire transmission_1_p3, transmission_1_p4;

  // Transmission_Gate transmission_1: pin names not known; wires that end beside it: in0, s0, transmission_1_p3, transmission_1_p4
  not not_1 (transmission_1_p3, s0);
  // Transmission_Gate transmission_2: pin names not known; wires that end beside it: in1, transmission_1_p3, s0, transmission_1_p4
  not not_2 (z, transmission_1_p4);

  // Notes on the sheet:
  //   2-1 Transmission Multiplexer
  //   01/08/2025
  //   Ryan Kellar
endmodule

module mx4i (
  input  d00,
  input  d01,
  input  d10,
  input  s1,
  input  d11,
  input  s0,
  output O
);

  wire mx2i_1_z, mx2i_2_z;

  mx2i mx2i_1 (.s0(s0), .in1(d01), .in0(d00), .z(mx2i_1_z));
  mx2i mx2i_2 (.s0(s0), .in1(d11), .in0(d10), .z(mx2i_2_z));
  mx2i mx2i_3 (.s0(s1), .in1(mx2i_2_z), .in0(mx2i_1_z), .z(O));

  // Notes on the sheet:
  //   4-1 Transmission Multiplexer
  //   01/08/2025
  //   Ryan Kellar
  //   z = max(d00+2, d01+2, d10+2, d11+2, s0+2.75, s1+1.75)
endmodule

module FAO2 (
  input  a,
  input  b,
  input  Cin,
  output S,
  output Cout
);

  wire and_1_out, nand_1_out, nand_2_out, nand_3_out, nor_1_out, nor_2_out, nor_3_out, not_1_out;

  nor nor_1 (nor_1_out, a, b);
  not not_1 (not_1_out, nand_1_out);
  nand nand_1 (nand_1_out, a, b);
  nor nor_2 (nor_2_out, nor_1_out, not_1_out);
  nand nand_2 (nand_2_out, a, Cin);
  nand nand_3 (nand_3_out, b, Cin);
  nor nor_3 (nor_3_out, nor_2_out, Cin);
  and and_1 (and_1_out, nor_2_out, Cin);
  nand nand_4 (Cout, nand_1_out, nand_2_out, nand_3_out);
  nor nor_4 (S, nor_3_out, and_1_out);

  // Notes on the sheet:
  //   1.00
  //   1.00
  //   1.00
  //   0.75
  //   1.00
  //   1.75
  //   1.00
  //   1.25
  //   1.00
  //   1.00
  //   Ryan Kellar
  //   12/14/2024
  //   42 transistors
  //   1.00 + 0.75 + 1.00 + 1.75 + 1.00 = 5.5
  //   If Cin < 2.75 then 5.5 else Cin + 2.75
  //   1.00 + 1.25 = 2.25
  //   Cin + 2.25
endmodule

module AOI21 (
  input  in_1,
  input  in_2,
  input  in_3,
  output out_4
);

  wire and_1_out;

  and and_1 (and_1_out, in_1, in_2);
  nor nor_1 (out_4, and_1_out, in_3);
endmodule

module determiningoverflow (
  input  A,
  input  B,
  input  R,
  input  op,
  output overflow
);

  wire multiplexer_1_out, not_1_out, not_2_out, xor_1_out, xor_2_out;

  not not_1 (not_1_out, B);
  Multiplexer multiplexer_1 (.in0(B), .in1(not_1_out), .out(multiplexer_1_out), .sel(op));
  xor xor_1 (xor_1_out, A, multiplexer_1_out);
  not not_2 (not_2_out, xor_1_out);
  xor xor_2 (xor_2_out, multiplexer_1_out, R);
  and and_1 (overflow, not_2_out, xor_2_out);
endmodule

module RegisterOp (
  input  clck,
  input  reset,
  input  [3:0] op,
  input  [1:0] Rd,
  input  [1:0] Rs,
  output [15:0] a,
  output [15:0] b,
  output [15:0] reg0,
  output [15:0] reg1,
  output [15:0] reg2,
  output [15:0] reg3
);

  wire nor_1_out, not_1_out, not_2_out, ovrfl, register_1_q, regwe_1_reg0we, regwe_1_reg1we, regwe_1_reg2we,
       regwe_1_reg3we;
  wire [15:0] sixteenbitaddsubtract_1_s;

  not not_1 (not_1_out, op[0]);
  not not_2 (not_2_out, op[1]);
  nor nor_1 (nor_1_out, not_1_out, not_2_out, op[2], op[3]);
  Register #(.width(1)) register_1 (.D(1'b1), .en(ovrfl), .clk(clck), .Q(register_1_q), .clr(reset));
  LED led_1 (.in(register_1_q));
  SixteenBitAddSubtract sixteenbitaddsubtract_1 (
    .a(a), .b(b), .op(nor_1_out), .overflow(ovrfl), .S(sixteenbitaddsubtract_1_s));
  srcSel srcsel_1 (.sel(Rd), .reg0(reg0), .reg1(reg1), .reg2(reg2), .reg3(reg3), .regOut(a));
  srcSel srcsel_2 (.sel(Rs), .reg0(reg0), .reg1(reg1), .reg2(reg2), .reg3(reg3), .regOut(b));
  regWE regwe_1 (
    .Rd(Rd), .regWrite(1'b1), .reg0WE(regwe_1_reg0we), .reg1WE(regwe_1_reg1we), .reg2WE(regwe_1_reg2we),
    .reg3WE(regwe_1_reg3we));
  Register #(.width(16)) R0 (.D(sixteenbitaddsubtract_1_s), .en(regwe_1_reg0we), .clk(clck), .Q(reg0), .clr(reset));
  Register #(.width(16)) R1 (.D(sixteenbitaddsubtract_1_s), .en(regwe_1_reg1we), .clk(clck), .Q(reg1), .clr(reset));
  Register #(.width(16)) R2 (.D(sixteenbitaddsubtract_1_s), .en(regwe_1_reg2we), .clk(clck), .Q(reg2), .clr(reset));
  Register #(.width(16)) R3 (.D(sixteenbitaddsubtract_1_s), .en(regwe_1_reg3we), .clk(clck), .Q(reg3), .clr(reset));

  // Other names for the same wires on the sheet: clk = clck; R0[15:0] = reg0; R1[15:0] = reg1; R2[15:0] = reg2;
  //   R3[15:0] = reg3; rst = reset
endmodule

module srcSel (
  input  [1:0] sel,
  input  [15:0] reg0,
  input  [15:0] reg1,
  input  [15:0] reg2,
  input  [15:0] reg3,
  output [15:0] regOut
);

  wire [15:0] multiplexer_1_out, multiplexer_2_out;

  Multiplexer #(.width(16)) multiplexer_1 (.in0(reg0), .in1(reg1), .out(multiplexer_1_out), .sel(sel[0]));
  Multiplexer #(.width(16)) multiplexer_2 (.in0(reg2), .in1(reg3), .out(multiplexer_2_out), .sel(sel[0]));
  Multiplexer #(.width(16)) multiplexer_3 (
    .in0(multiplexer_1_out), .in1(multiplexer_2_out), .out(regOut), .sel(sel[1]));
endmodule

module regWE (
  input  [1:0] Rd,
  input  regWrite,
  output reg0WE,
  output reg1WE,
  output reg2WE,
  output reg3WE
);

  wire not_1_out, not_2_out;

  not not_1 (not_1_out, Rd[0]);
  not not_2 (not_2_out, Rd[1]);
  and and_1 (reg0WE, not_1_out, regWrite, not_2_out);
  and and_2 (reg1WE, Rd[0], regWrite, not_2_out);
  and and_3 (reg2WE, not_1_out, regWrite, Rd[1]);
  and and_4 (reg3WE, Rd[0], regWrite, Rd[1]);
endmodule

module ProgramCounter (
  input  [5:0] targ,
  input  jmp,
  input  clk,
  input  rst,
  output [5:0] pc,
  output [5:0] cycle
);

  wire [5:0] adder_1_out, adder_2_out, multiplexer_1_out;

  Adder #(.width(6)) adder_1 (.a(pc), .b(6'b000001), .out(adder_1_out));  // open: cin, cout
  Register #(.width(6)) PCReg (.D(multiplexer_1_out), .en(1'b1), .clk(clk), .Q(pc), .clr(rst));
  Multiplexer #(.width(6)) multiplexer_1 (.in0(adder_1_out), .in1(targ), .out(multiplexer_1_out), .sel(jmp));
  Register #(.width(6)) register_1 (.D(adder_2_out), .en(1'b1), .clk(clk), .Q(cycle), .clr(rst));
  Adder #(.width(6)) adder_2 (.a(cycle), .b(6'b000001), .out(adder_2_out));  // open: cin, cout
endmodule

module LALU (
  input  in_1,
  output [5:0] cycle,
  output [7:0] out_3,
  output [15:0] a,
  output [15:0] b
);

  wire clk, irdecoder_1_add, irdecoder_1_sub, jmp, ld, ldi, mv, or_1_out, ovrfl, ovrfl_q, regwe_1_reg0we,
       regwe_1_reg1we, regwe_1_reg2we, regwe_1_reg3we, st;
  wire [1:0] irdecoder_1_rd, Rs;
  wire [5:0] programcounter_1_pc, targ;
  wire [7:0] programMemory_dout;
  wire [15:0] dataOut, multiplexer_1_out, multiplexer_2_out, R0, R1, R2, R3, sixteenbitaddsubtract_1_s;

  ProgramCounter programcounter_1 (
    .targ(targ), .jmp(jmp), .clk(clk), .rst(in_1), .pc(programcounter_1_pc), .cycle(cycle));
  RAM #(.addrWidth(6), .asyncread("true"), .trigger("falling")) programMemory (
    .addr(programcounter_1_pc), .we(1'b0), .oe(1'b1), .clk(clk), .dout(programMemory_dout));  // open: din
  Register InstructionRegister (.D(programMemory_dout), .en(1'b1), .clk(clk), .Q(out_3), .clr(in_1));
  IRDecoder irdecoder_1 (
    .IR(out_3), .clk(clk), .rst(in_1), .Rs(Rs), .Rd(irdecoder_1_rd), .add(irdecoder_1_add),
    .sub(irdecoder_1_sub), .ld(ld), .ldi(ldi), .mv(mv), .st(st), .jmp(jmp), .targ(targ));
  Clock clock_1 (.out(clk));
  or or_1 (or_1_out, ldi, ld, irdecoder_1_sub, irdecoder_1_add);
  Register #(.width(1)) u_ovrfl (.D(or_1_out), .en(ovrfl), .clk(clk), .Q(ovrfl_q), .clr(in_1));
  LED led_1 (.in(ovrfl_q));
  RAM #(.addrWidth(4), .asyncread("true"), .dataWidth(16), .trigger("falling")) dataMemory (
    .addr(b[3:0]), .we(st), .oe(1'b1), .clk(clk), .din(a), .dout(dataOut));
  SixteenBitAddSubtract sixteenbitaddsubtract_1 (
    .a(a), .b(b), .op(irdecoder_1_sub), .overflow(ovrfl), .S(sixteenbitaddsubtract_1_s));
  srcSel srcsel_1 (.sel(irdecoder_1_rd), .reg0(R0), .reg1(R1), .reg2(R2), .reg3(R3), .regOut(a));
  srcSel srcsel_2 (.sel(Rs), .reg0(R0), .reg1(R1), .reg2(R2), .reg3(R3), .regOut(b));
  regWE regwe_1 (
    .Rd(irdecoder_1_rd), .regWrite(or_1_out), .reg0WE(regwe_1_reg0we), .reg1WE(regwe_1_reg1we),
    .reg2WE(regwe_1_reg2we), .reg3WE(regwe_1_reg3we));
  Multiplexer #(.width(16)) multiplexer_1 (
    .in0(sixteenbitaddsubtract_1_s), .in1({{14{1'b0}}, Rs}), .out(multiplexer_1_out), .sel(ldi));
  Multiplexer #(.width(16)) multiplexer_2 (.in0(multiplexer_1_out), .in1(dataOut), .out(multiplexer_2_out), .sel(ld));
  Register #(.width(16)) u_R0 (.D(multiplexer_2_out), .en(regwe_1_reg0we), .clk(clk), .Q(R0), .clr(in_1));
  Register #(.width(16)) u_R1 (.D(multiplexer_2_out), .en(regwe_1_reg1we), .clk(clk), .Q(R1), .clr(in_1));
  Register #(.width(16)) u_R2 (.D(multiplexer_2_out), .en(regwe_1_reg2we), .clk(clk), .Q(R2), .clr(in_1));
  Register #(.width(16)) u_R3 (.D(multiplexer_2_out), .en(regwe_1_reg3we), .clk(clk), .Q(R3), .clr(in_1));
  Hex_Digit_Display hex_digit_display_1 (.value(R0[15:12]));  // open: dp
  Hex_Digit_Display hex_digit_display_2 (.value(R1[15:12]));  // open: dp
  Hex_Digit_Display hex_digit_display_3 (.value(R2[15:12]));  // open: dp
  Hex_Digit_Display hex_digit_display_4 (.value(R3[15:12]));  // open: dp
  Hex_Digit_Display hex_digit_display_5 (.value(R0[11:8]));  // open: dp
  Hex_Digit_Display hex_digit_display_6 (.value(R0[7:4]));  // open: dp
  Hex_Digit_Display hex_digit_display_7 (.value(R1[11:8]));  // open: dp
  Hex_Digit_Display hex_digit_display_8 (.value(R1[7:4]));  // open: dp
  Hex_Digit_Display hex_digit_display_9 (.value(R2[11:8]));  // open: dp
  Hex_Digit_Display hex_digit_display_10 (.value(R2[7:4]));  // open: dp
  Hex_Digit_Display hex_digit_display_11 (.value(R3[11:8]));  // open: dp
  Hex_Digit_Display hex_digit_display_12 (.value(R3[7:4]));  // open: dp
  Hex_Digit_Display hex_digit_display_13 (.value(R0[3:0]));  // open: dp
  Hex_Digit_Display hex_digit_display_14 (.value(R1[3:0]));  // open: dp
  Hex_Digit_Display hex_digit_display_15 (.value(R2[3:0]));  // open: dp
  Hex_Digit_Display hex_digit_display_16 (.value(R3[3:0]));  // open: dp

  // Other names for the same wires on the sheet: rst = in_1

  // Notes on the sheet:
  //   LALU: LASA Arithmetic Logic Unit by Ryan Kellar '25
  //   LASA{CS} --> 4C 41 53 41 7B 43 53 7D
  //   LASA{CS} Operations:
  //   10 11 0011 = b3 -> R2=R2-R3
  //   01 00 0011 = 43 -> R1=R1-R0
  //   11 10 0010 = e2 -> R3=R3+R2
  //   00 11 0010 = 32 -> R0=R0+R3
  //   10 00 0010 = 82 -> R2=R2+R0
  //   Data Memory:
  //   Instruction Memory:
  //   Instruction Memory:
  //   First 4 Instructions
  //   000f 00fc 0fde 6f15 70eb f022 ff04 ffff
  //   Fibonacci Instructions
  //   0e ce 5e 9e 8f e2 12 8f e2 12 8f e2 12 8f e2 12 8f e3 12 8f e3 12 8f e3 12 8f e3 12
  //   8e 5e ee 1e 6b cb 32 3b b2 82 8b c2 c2 8f 12 cb b2 cf 12 8b e2 8f 12 cb b2 cf 12 8b e2 8f 12 cb b2 12 8b 00 00 00 00 00 00 00 00 00 00 00 00 00 00 00 00 00 00 00 00 00 00 00 00 00 00 00 00 00
endmodule

module OpDecoder (
  input  [3:0] opcode,
  output add,
  output sub,
  output ld,
  output ldi,
  output mv,
  output st,
  output jmp
);

  wire not_1_out, not_2_out, not_3_out, not_4_out, not_5_out, not_6_out, or_1_out;

  not not_1 (not_1_out, opcode[1]);
  not not_2 (not_2_out, opcode[0]);
  not not_3 (not_3_out, opcode[0]);
  not not_4 (not_4_out, opcode[3]);
  not not_5 (not_5_out, opcode[2]);
  or or_1 (or_1_out, opcode[3], not_1_out, opcode[2]);
  not not_6 (not_6_out, opcode[0]);
  and and_1 (ld, opcode[2], opcode[3], opcode[0], opcode[1]);
  and and_2 (ldi, opcode[1], not_2_out, opcode[3], opcode[2]);
  and and_3 (mv, not_3_out, opcode[1], opcode[2], not_4_out);
  and and_4 (st, opcode[0], opcode[1], not_5_out, opcode[3]);
  nor nor_1 (jmp, opcode[0], opcode[1]);
  nor nor_2 (add, opcode[0], or_1_out);
  nor nor_3 (sub, or_1_out, not_6_out);
endmodule

module IRDecoder (
  input  [7:0] IR,
  input  clk,
  input  rst,
  output [1:0] Rs,
  output [1:0] Rd,
  output add,
  output sub,
  output ld,
  output ldi,
  output mv,
  output st,
  output jmp,
  output [5:0] targ
);

  wire and_1_out, FV_q, opdecoder_1_add, opdecoder_1_jmp, opdecoder_1_ld, opdecoder_1_ldi, opdecoder_1_mv,
       opdecoder_1_st, opdecoder_1_sub;

  Register #(.width(2)) RegD (.D(IR[7:6]), .en(1'b1), .clk(clk), .Q(Rd), .clr(rst));
  Register #(.width(2)) RegS (.D(IR[5:4]), .en(1'b1), .clk(clk), .Q(Rs), .clr(rst));
  D_Flip_Flop FV (.D(1'b1), .clk(clk), .Q(FV_q), .reset(rst));  // open: Qn, preset
  and and_1 (and_1_out, FV_q, opdecoder_1_jmp);
  OpDecoder opdecoder_1 (
    .opcode(IR[3:0]), .add(opdecoder_1_add), .sub(opdecoder_1_sub), .ld(opdecoder_1_ld),
    .ldi(opdecoder_1_ldi), .mv(opdecoder_1_mv), .st(opdecoder_1_st), .jmp(opdecoder_1_jmp));
  D_Flip_Flop RegAdd (.D(opdecoder_1_add), .clk(clk), .Q(add), .reset(rst));  // open: Qn, preset
  D_Flip_Flop RegSub (.D(opdecoder_1_sub), .clk(clk), .Q(sub), .reset(rst));  // open: Qn, preset
  D_Flip_Flop RegLoad (.D(opdecoder_1_ld), .clk(clk), .Q(ld), .reset(rst));  // open: Qn, preset
  D_Flip_Flop RegLoadImmediate (.D(opdecoder_1_ldi), .clk(clk), .Q(ldi), .reset(rst));  // open: Qn, preset
  D_Flip_Flop RegMove (.D(opdecoder_1_mv), .clk(clk), .Q(mv), .reset(rst));  // open: Qn, preset
  D_Flip_Flop RegStore (.D(opdecoder_1_st), .clk(clk), .Q(st), .reset(rst));  // open: Qn, preset
  D_Flip_Flop RegJump (.D(and_1_out), .clk(clk), .Q(jmp), .reset(rst));  // open: Qn, preset

  assign targ = IR[7:2];

  // Other names for the same wires on the sheet: c = clk; tg[5:0] = IR[7:2]; r = rst
endmodule
